# Fritzing sketch esquema_ligacoes (saved by Fritzing 1.0.4)

parts:
  A1 = ESP32-pico-kit-v4 [part_number=ESP32--pico-kit-v4]
  Componente1 = Adafruit BME680 [part_number="Adafruit #3660"]
  Mod1 = SDS011 - dust sensor [part_number=1]

nets:
  GND: A1.Pin_19, A1.Pin_22, Componente1.GND, Mod1.GND
  N1: A1.Pin_20, Mod1.5V
  N2: A1.Pin_21, Componente1.VCC
  N3: A1.Pin_28, Mod1.RXD
  N4: A1.Pin_29, Mod1.TXD
  N5: A1.Pin_36, Componente1.SCK/SCL
  N6: A1.Pin_37, Componente1.SDI/SDA

custom parts:
  ESP32-pico-kit-v4: ESP32-PICO-KIT is a mini development board produced by Espressif. At the core of this board is the ESP32-PICO-D4, a System-in-Package (SiP) module with complete Wi-Fi and Bluetooth functionalities.
  SDS011 - dust sensor: The SDS 011 Sensor is a quite recent Air Quality Sensor developed by inovafit, a spin-off from the university of Jinan (in Shandong). With its size, it is probably one of the best sensor in terms of accuracy: While other sensors tend to focus on shrinking the sensor size, the SDS 011 has opted for a size tradeoff allowing it to use a larger fan. And the larger the fan, the better the quality.
